// Digital circuit fact-controller.dig as structural Verilog
module fact_controller (
  input  clk,
  input  rst,
  input  start,
  input  n_lt_2,
  input  [7:0] \continue ,
  output sel_r,
  output load_r,
  output [1:0] sel_n,
  output load_n,
  output [1:0] sel_c,
  output load_c,
  output [1:0] sel_s,
  output push,
  output pop,
  output finish,
  output [7:0] state
);

  fib_controller #(.applicationType("IVERILOG")) u_fib_controller (
    .clk(clk), .rst(rst), .start(start), .nless2(n_lt_2), .\continue (\continue ), .sel_r(sel_r),
    .load_r(load_r), .load_n(load_n), .load_c(load_c), .push(push), .pop(pop), .finish(finish),
    .state(state[4:0]), .sel_n(sel_n), .sel_c(sel_c), .sel_s(sel_s));
  // Pins of 5 and 8 bits meet at state
endmodule

/* Code of fib_controller:
/*
	state	 next 	                  output
       ======= ========================== =========
	s0    if start then s1 else s0    	n <- input
	s1    loop			  continue <- fib-done
12	loop: if n < 2 then fib-base 
              else s2
	s2:   s3			 push continue
	s3:   s4			 push n
	s4:   loop			 n<-n-1, continue <- after-fib-n-1
13 	after-fib-n-1: s5			 n <- stack
	s5:   s6			 pop
	s6:   s7		 	 push r
	s7:   loop			 n <- n-2, continue <- after-fib-n-2
14	after-fib-n-2:   s8			 n <- stack (fib n-1)
	s8:   s9			 pop
	s9:   s10			continue <- stack
	s10: s11			pop
	s11: next <- continue	 r <- r + n			 

15   fib-base:    next <- continue	 r <- n
16   fib-done: 			 finish <- 1
* /

module fib_controller(
	clk, rst, start,nless2, continue,
	sel_r, load_r, sel_n, load_n, sel_c, load_c, sel_s, push,pop, finish, state
);

	input clk, rst, start,nless2;
	input [7:0] continue;
	output sel_r, load_r,  load_n,  load_c, push, pop, finish;
	output [4:0] state;
	output [1:0] sel_n, sel_c, sel_s;

	reg [4:0] state, next;

	reg [1:0] sel_n, sel_c, sel_s;

	assign finish = (state == 16)? 1 : 0;
	
	assign push = (state==2 || state==3 || state==6)?1:0;
	assign pop = (state == 5 || state == 8 || state == 10) ? 1 : 0;
	
	assign sel_r = (state == 11)?0:1;
	assign load_r = (state == 15 || state == 11)?1:0;
	assign load_n = (state == 0 || state == 4 || state == 7|| state == 13|| state == 14) ? 1 : 0;

	always @(state)
	begin
		case(state)
			3: sel_s = 0;
			2: sel_s = 1;
			6: sel_s = 2;
			default: sel_s = 3;
		endcase
	end

	always @(state)
	begin
		case(state)
			0: sel_n = 1;
			4: sel_n = 0;
			7: sel_n = 3;
			13: sel_n = 2;
			14 :sel_n = 2;
			default: sel_n = 1;
		endcase
	end

	assign load_c = (state == 1 || state == 4 || state == 7|| state == 9)?1:0;
	always @(state)
	begin
		case(state)
			1: sel_c = 0;
			4: sel_c = 1;
			9: sel_c = 2;
			7: sel_c = 3;
			default: sel_c = 0;
		endcase
	end

	always @(state or start or nless2 or continue)
	begin
		case(state)
			0: if(start)
				next = 1;
			   else
				next = 0;
			1: next = 12;
			12: if(nless2)
				next = 15;
			    else
				next = 2;
			2:  next = 3;
			3: next = 4;
			4: next = 12;
			13: next = 5;
			5: next = 6;
			6: next = 7;
			7: next = 12;
			14: next = 8;
			8: next = 9;
			9: next = 10;
			10: next = 11;
			11: next = continue;
			15: next = continue;
			16: next = 16;
			default: next = 0;
		endcase
	end

	always @(posedge clk)
	begin
		if(rst)
			state = 0;
		else
			state = next;
	end

	
endmodule
*/
