// Digital circuit fib2.dig as structural Verilog
module fib2 (
  input  clk,
  input  rst,
  input  start,
  input  [7:0] n,
  input  clk_2,
  output [7:0] result,
  output finish
);

  wire comparator_1_lt, fact_controller_1_load_c, fact_controller_1_load_n, fact_controller_1_load_r,
       fact_controller_1_pop, fact_controller_1_push, fact_controller_1_sel_r;
  wire [1:0] fact_controller_1_sel_c, fact_controller_1_sel_n, fact_controller_1_sel_s;
  wire [7:0] add_1_s, continue_q, fact_controller_1_state, multiplexer_1_out, multiplexer_2_out,
       multiplexer_3_out, multiplexer_4_out, n_q, stack_1_dout, sub_1_s, sub_2_s;

  // Probe on fact_controller_1_sel_n
  // Probe on comparator_1_lt
  Multiplexer #(.Bits(8)) multiplexer_1 (
    .sel(fact_controller_1_sel_r), .in_0(add_1_s), .in_1(n_q), .out(multiplexer_1_out));
  Multiplexer #(.Selector_Bits(2), .Bits(8)) multiplexer_2 (
    .sel(fact_controller_1_sel_n), .in_0(sub_1_s), .in_1(n), .in_2(stack_1_dout), .in_3(sub_2_s),
    .out(multiplexer_2_out));
  Multiplexer #(.Selector_Bits(2), .Bits(8)) multiplexer_3 (
    .sel(fact_controller_1_sel_c), .in_0(8'h10), .in_1(8'hd), .in_2(stack_1_dout), .in_3(8'he),
    .out(multiplexer_3_out));
  Multiplexer #(.Selector_Bits(2), .Bits(8)) multiplexer_4 (
    .sel(fact_controller_1_sel_s), .in_0(n_q), .in_1(continue_q), .in_2(result), .in_3({8{1'b0}}),
    .out(multiplexer_4_out));
  Register #(.Bits(8)) r (.D(multiplexer_1_out), .C(clk_2), .en(fact_controller_1_load_r), .Q(result));
  Register #(.Bits(8)) u_n (.D(multiplexer_2_out), .C(clk_2), .en(fact_controller_1_load_n), .Q(n_q));
  Register #(.Bits(8)) \continue  (.D(multiplexer_3_out), .C(clk_2), .en(fact_controller_1_load_c), .Q(continue_q));
  stack stack_1 (
    .clk(clk_2), .rst(rst), .push(fact_controller_1_push), .pop(fact_controller_1_pop),
    .din(multiplexer_4_out), .dout(stack_1_dout));  // open: empty
  fact_controller fact_controller_1 (
    .clk(clk_2), .rst(rst), .start(start), .n_lt_2(comparator_1_lt), .\continue (continue_q),
    .sel_r(fact_controller_1_sel_r), .load_r(fact_controller_1_load_r), .sel_n(fact_controller_1_sel_n),
    .state(fact_controller_1_state), .load_n(fact_controller_1_load_n), .sel_c(fact_controller_1_sel_c),
    .load_c(fact_controller_1_load_c), .sel_s(fact_controller_1_sel_s), .push(fact_controller_1_push),
    .pop(fact_controller_1_pop), .finish(finish));
  // Probe on n_q
  Add #(.Bits(8)) add_1 (.a(result), .b(n_q), .c_i(1'b0), .s(add_1_s));  // open: c_o
  Sub #(.Bits(8)) sub_1 (.a(n_q), .b(8'h1), .c_i(1'b0), .s(sub_1_s));  // open: c_o
  Sub #(.Bits(8)) sub_2 (.a(n_q), .b(8'h2), .c_i(1'b0), .s(sub_2_s));  // open: c_o
  Comparator #(.Bits(8)) comparator_1 (.a(n_q), .b(8'h2), .lt(comparator_1_lt));  // open: gt, eq
  // Probe on fact_controller_1_state

  // Notes on the sheet:
  //   clk_2: Hz: 20
endmodule
