// Digital circuit stack.dig as structural Verilog
module stack (
  input  clk,
  input  rst,
  input  push,
  input  pop,
  input  [7:0] din,
  output [7:0] dout,
  output empty
);

  stack #(.applicationType("IVERILOG")) u_stack (
    .clk(clk), .rst(rst), .push(push), .pop(pop), .din(din), .dout(dout), .empty(empty));
endmodule

/* Code of stack:
module stack(clk, rst, push, pop, din, dout, empty);
	input clk, rst, push, pop;
	input [7:0] din;
	output [7:0] dout;
	output empty;

	reg [7:0] data[0:255];

	reg [7:0] top;

	always @(posedge clk)
	begin
		if(rst)
			top = 0;
		else if(pop && ~empty)
			top = top - 1;
		else if(push)
		begin
			top = top + 1;
			data[top] = din;
		end
	end

	assign empty = (top == 0)?1:0;
	assign dout = data[top];
	
endmodule
*/
